# Fritzing sketch diagram (saved by Fritzing 1.0.3b)
breadboards: 1

parts:
  U1 = 7-SEGMENT-DISPLAY [package=7-segment-display]
  Mod1 = Raspberry Pi 4B
  R1 = Resistor [tolerance=±5% power=0.25W resistance=220 package=THT]
  R2 = Resistor [tolerance=±5% power=0.25W resistance=220 package=THT]
  R3 = Resistor [tolerance=±5% power=0.25W resistance=220 package=THT]
  R4 = Resistor [tolerance=±5% power=0.25W resistance=220 package=THT]
  R5 = Resistor [tolerance=±5% power=0.25W resistance=220 package=THT]
  R6 = Resistor [tolerance=±5% power=0.25W resistance=220 package=THT]
  R7 = Resistor [tolerance=±5% power=0.25W resistance=220 package=THT]
  R8 = Resistor [tolerance=±5% power=0.25W resistance=220 package=THT]
  IC1 = L293D [package=THT]
  PSU1 = Adjustable Breadboard Power Supply
  M1 = DC Motor [voltage_(max)=6V voltage_(min)=3V]
  J1 = Basic Servo
  S1 = Pushbutton [package="[SMD]"]
  S2 = Pushbutton [package="[SMD]"]

nets:
  N1: U1.E, R8.Pin_1
  N2: U1.D, R2.Pin_1
  N3: U1.G1, R1.Pin_1
  N4: U1.C, U1.F, Mod1.3V3, IC1.0V
  N5: U1.DP, R3.Pin_0
  N6: U1.B, R4.Pin_0
  N7: U1.A, R6.Pin_0
  N8: U1.G2, R5.Pin_0
  N9: U1.G, R7.Pin_1
  GND: Mod1.GND, PSU1.Vin-, J1.gnd, S1.Pin_1, S1.Pin_2, S2.Pin_1, S2.Pin_2
  N10: Mod1.GPIO18, J1.pulse
  N11: Mod1.GPIO27, IC1.In_2
  N12: Mod1.GPIO22, IC1.In_1
  N13: Mod1.GPIO25, S1.Pin_3, S1.Pin_4
  N14: Mod1.GPIO5, S2.Pin_3, S2.Pin_4
  N15: Mod1.GPIO6, R6.Pin_1
  N16: Mod1.GPIO12, R7.Pin_0
  N17: Mod1.GPIO13, R4.Pin_1
  N18: Mod1.GPIO19, R3.Pin_1
  N19: Mod1.GPIO16, R5.Pin_1
  N20: Mod1.GPIO26, R8.Pin_0
  N21: Mod1.GPIO20, R2.Pin_0
  N22: Mod1.GPIO21, R1.Pin_0
  N23: IC1.Enable_1, IC1.+Vmotor, PSU1.Vout+, J1.vcc
  N24: IC1.Out_1_(_Controlled_by_Enable_1_), M1.pin_2
  N25: IC1.Out_2_(_Controlled_by_Enable_1_), M1.pin_1
